# Fritzing sketch Robopot (saved by Fritzing 0.9.4)
breadboards: 1

parts:
  Argon1 = Particle Argon
  M1 = BMP280
  OLED_I2C1 = OLED 128x64 I2C Monochrome Display
  Grove1 = Grove Dust Sensor
  SENS1 = SoilWatch 10
  Part1 = MQ-131 breakout
  Relay1 = Relay - 6 pins [package="DIP (Dual Inline) [THT]"]

nets:
  VCC: Argon1.3.3V, OLED_I2C1.VDD, Grove1.VCC, SENS1.VCC, Part1.VCC, Relay1.VCC
  GND: Argon1.GND, OLED_I2C1.GND, Grove1.GND, SENS1.OUT, Part1.GND, Relay1.GND
  N1: Argon1.A0, Grove1.NC
  N2: Argon1.A1, SENS1.GND
  N3: Argon1.A2, Part1.DO
  N4: Argon1.A3, Relay1.IN
  N5: Argon1.SDA, M1.SDA, OLED_I2C1.SDA
  N6: Argon1.SCL, M1.SCL, OLED_I2C1.SCK

custom parts:
  Particle Argon: The Argon is a powerful Wi-Fi enabled development board that can act as either a standalone Wi-Fi endpoint or Wi-Fi enabled gateway for Particle Mesh networks. It is based on the Nordic nRF52840 and has built-in battery charging circuitry so it’s easy to connect a Li-Po and deploy your local network in minutes. The Argon is great for connecting existing projects to the Particle Device Cloud or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
  BMP280: Temperature Humidity Barometric presure Sensor, I2C
  Grove Dust Sensor: PPD42 Grove Dust Sensor
  SoilWatch 10: SoilWatch 10 - Capacitive soil moisture sensor
  MQ-131 breakout: SKU: 101282
  Relay - 6 pins: A DIP stand-in part for whatever IC you want. With 6 pins on a 900mil dual inline package (DIP) footprint.
